# Fritzing sketch TestBoard (saved by Fritzing 0.9.3b)
breadboards: 1

parts:
  Part1 = Arduino Pro Mini v13
  U1 = ENCODER-QUADRATURE [package=encoder-16mm-quad]
  S1 = Momentary Switch [package=ksa_sealed_tac_switch]
  Grove1 = Grove OLED 128x96

nets:
  N1: Part1.A4, Grove1.SDA
  N2: Part1.A5, Grove1.SCL
  GND: Part1.GND, U1.C, S1.2, S1.4, Grove1.GND
  VCC: Part1.VCC, Grove1.VCC
  N3: Part1.D12/MISO, S1.1, S1.3
  N4: Part1.D11_PWM/MOSI, U1.B
  N5: Part1.D10_PWM/SS, U1.A
